# Fritzing sketch ControladorLEDsCocina (saved by Fritzing 0.9.3b)

parts:
  12V = Screw terminal - 2 pins [package=THT]
  12V_>_5V = RioRand LM2596
  WeMos_D1_Mini1 = WeMos D1 Mini
  Componente1 = I2C level shifter bidirectional
  KY-1 = Keyes Relay [package=THT]
  Tira1 = Screw terminal - 2 pins [package=THT]
  KY-2 = Keyes Relay [package=THT]
  Tira2 = Screw terminal - 2 pins [package=THT]
  KY-3 = Keyes Relay [package=THT]
  KY-4 = Keyes Relay [package=THT]
  Tira3 = Screw terminal - 2 pins [package=THT]
  Tira4 = Screw terminal - 2 pins [package=THT]
  Componente2 = HC-SR501 Body Sensor Module
  R2 = Resistor [tolerance=±5% resistance=1k package=THT]
  R3 = Resistor [tolerance=±5% resistance=1k package=THT]

nets:
  N1: 12V.pin1, 12V_>_5V.Pin_2, Tira1.pin1, Tira2.pin1, Tira3.pin1, Tira4.pin1
  N2: 12V.pin2, 12V_>_5V.Pin_1, KY-1.C, KY-2.C, KY-3.C, KY-4.C
  5V: 12V_>_5V.Pin_3, WeMos_D1_Mini1.5V, Componente1.HV, KY-1.power, Componente2.VCC
  GND: 12V_>_5V.Pin_4, WeMos_D1_Mini1.G, Componente1.GND, KY-1.ground, Componente2.GND, R2.Pin_1
  N3: WeMos_D1_Mini1.3V3, Componente1.LV
  N4: WeMos_D1_Mini1.D1, Componente1.LV4
  N5: WeMos_D1_Mini1.D2, Componente1.LV3
  N6: WeMos_D1_Mini1.D3, Componente1.LV2
  N7: WeMos_D1_Mini1.D4, Componente1.LV1
  N8: WeMos_D1_Mini1.D8, R3.Pin_0
  N9: Componente1.HV1, KY-1.signal
  N10: Componente1.HV2, KY-2.signal
  N11: Componente1.HV3, KY-3.signal
  N12: Componente1.HV4, KY-4.signal
  N13: KY-1.NO, Tira1.pin2
  N14: KY-2.NO, Tira2.pin2
  N15: KY-3.NO, Tira3.pin2
  N16: KY-4.NO, Tira4.pin2
  N17: Componente2.OUT, R3.Pin_1

custom parts:
  Keyes Relay: The Keyes 5V relay module is suitable for SCM development, home appliance control. It uses a 5V~12V TIL control signal which can control DC / AC signal.
  HC-SR501 Body Sensor Module: Pyroelectric Infrared PIR Motion Sensor Detector Module
