# Fritzing sketch ControladorLEDsCocina_SSR (saved by Fritzing 0.9.3b)

parts:
  12V = Screw terminal - 2 pins [package=THT]
  12V_>_5V = RioRand LM2596
  WeMos_D1_Mini1 = WeMos D1 Mini
  Componente1 = I2C level shifter bidirectional
  Tira1 = Screw terminal - 2 pins [package=THT]
  Tira2 = Screw terminal - 2 pins [package=THT]
  Tira3 = Screw terminal - 2 pins [package=THT]
  Tira4 = Screw terminal - 2 pins [package=THT]
  Componente2 = HC-SR501 Body Sensor Module
  R2 = Resistor [tolerance=±5% resistance=1k package=THT]
  R3 = Resistor [tolerance=±5% resistance=1k package=THT]
  Componente3 = Solid State High Level Relay Module [package=relay]
  Componente4 = Solid State High Level Relay Module [package=relay]
  Componente5 = Solid State High Level Relay Module [package=relay]
  Componente6 = Solid State High Level Relay Module [package=relay]

nets:
  N1: 12V.pin1, 12V_>_5V.Pin_2, Tira1.pin1, Tira2.pin1, Tira3.pin1, Tira4.pin1
  N2: 12V.pin2, 12V_>_5V.Pin_1, Componente3.A1, Componente4.A1, Componente5.A1, Componente6.A1
  5V: 12V_>_5V.Pin_3, WeMos_D1_Mini1.5V, Componente1.HV, Componente2.VCC, Componente3.DC+, Componente4.DC+, Componente5.DC+, Componente6.DC+
  GND: 12V_>_5V.Pin_4, WeMos_D1_Mini1.G, Componente1.GND, Componente2.GND, R2.Pin_1, Componente3.DC-, Componente4.DC-, Componente5.DC-, Componente6.DC-
  N3: WeMos_D1_Mini1.3V3, Componente1.LV
  N4: WeMos_D1_Mini1.D1, Componente1.LV4
  N5: WeMos_D1_Mini1.D2, Componente1.LV3
  N6: WeMos_D1_Mini1.D3, Componente1.LV2
  N7: WeMos_D1_Mini1.D4, Componente1.LV1
  N8: WeMos_D1_Mini1.D8, R3.Pin_0
  N9: Componente1.HV1, Componente3.CH1
  N10: Componente1.HV2, Componente4.CH1
  N11: Componente1.HV3, Componente5.CH1
  N12: Componente1.HV4, Componente6.CH1
  N13: Tira1.pin2, Componente3.B1
  N14: Tira2.pin2, Componente4.B1
  N15: Tira3.pin2, Componente5.B1
  N16: Tira4.pin2, Componente6.B1
  N17: Componente2.OUT, R3.Pin_1

custom parts:
  HC-SR501 Body Sensor Module: Pyroelectric Infrared PIR Motion Sensor Detector Module
  Solid State High Level Relay Module: 5V Omron solid state relay 240V 2A output with resistance fuse.
